// Logisim project ItsyBitsy.circ as structural Verilog: 1 circuit, main circuit main
module main (
  output [7:0] out_1,
  output [7:0] out_2,
  output [7:0] out_3,
  output [7:0] out_4
);

  wire and_1_out, and_2_out, and_3_out, and_4_out, clock_1_out, decoder_1_out0, decoder_1_out1,
       decoder_1_out2, decoder_1_out3, nor_1_out, not_1_out, not_2_out, or_1_out, or_2_out, xor_1_out;
  wire [7:0] adder_1_out, adder_2_out, multiplexer_3_out, multiplexer_4_out, multiplier_1_out, ram_1_dout,
       register_1_q, register_2_q, register_3_q, register_4_q, register_5_q;

  Clock clock_1 (.out(clock_1_out));
  LED led_1 (.in(clock_1_out));
  Decoder #(.select(2)) decoder_1 (
    .out0(decoder_1_out0), .out1(decoder_1_out1), .out2(decoder_1_out2), .out3(decoder_1_out3),
    .sel(ram_1_dout[5:4]));  // open: en
  LED led_2 (.in(clock_1_out));
  LED led_3 (.in(clock_1_out));
  LED led_4 (.in(clock_1_out));
  LED led_5 (.in(clock_1_out));
  LED led_6 (.in(clock_1_out));
  LED led_7 (.in(clock_1_out));
  LED led_8 (.in(clock_1_out));
  LED led_9 (.in(clock_1_out));
  LED led_10 (.in(clock_1_out));
  LED led_11 (.in(clock_1_out));
  LED led_12 (.in(decoder_1_out0));
  LED led_13 (.in(decoder_1_out2));
  LED led_14 (.in(clock_1_out));
  LED led_15 (.in(clock_1_out));
  LED led_16 (.in(clock_1_out));
  LED led_17 (.in(clock_1_out));
  LED led_18 (.in(clock_1_out));
  LED led_19 (.in(clock_1_out));
  LED led_20 (.in(clock_1_out));
  LED led_21 (.in(clock_1_out));
  LED led_22 (.in(clock_1_out));
  LED led_23 (.in(clock_1_out));
  LED led_24 (.in(clock_1_out));
  LED led_25 (.in(clock_1_out));
  LED led_26 (.in(clock_1_out));
  LED led_27 (.in(clock_1_out));
  LED led_28 (.in(clock_1_out));
  LED led_29 (.in(clock_1_out));
  LED led_30 (.in(clock_1_out));
  LED led_31 (.in(clock_1_out));
  LED led_32 (.in(clock_1_out));
  LED led_33 (.in(clock_1_out));
  LED led_34 (.in(clock_1_out));
  LED led_35 (.in(clock_1_out));
  LED led_36 (.in(clock_1_out));
  LED led_37 (.in(clock_1_out));
  LED led_38 (.in(clock_1_out));
  LED led_39 (.in(clock_1_out));
  LED led_40 (.in(clock_1_out));
  LED led_41 (.in(clock_1_out));
  LED led_42 (.in(clock_1_out));
  LED led_43 (.in(clock_1_out));
  LED led_44 (.in(clock_1_out));
  LED led_45 (.in(clock_1_out));
  LED led_46 (.in(clock_1_out));
  LED led_47 (.in(clock_1_out));
  LED led_48 (.in(clock_1_out));
  LED led_49 (.in(clock_1_out));
  LED led_50 (.in(clock_1_out));
  LED led_51 (.in(clock_1_out));
  LED led_52 (.in(clock_1_out));
  LED led_53 (.in(clock_1_out));
  LED led_54 (.in(clock_1_out));
  LED led_55 (.in(clock_1_out));
  Register register_1 (.D(adder_1_out), .en(1'b1), .clk(clock_1_out), .Q(register_1_q));  // open: clr
  LED led_56 (.in(clock_1_out));
  LED led_57 (.in(clock_1_out));
  LED led_58 (.in(clock_1_out));
  LED led_59 (.in(clock_1_out));
  LED led_60 (.in(clock_1_out));
  LED led_61 (.in(clock_1_out));
  LED led_62 (.in(clock_1_out));
  LED led_63 (.in(clock_1_out));
  LED led_64 (.in(clock_1_out));
  LED led_65 (.in(clock_1_out));
  LED led_66 (.in(clock_1_out));
  LED led_67 (.in(clock_1_out));
  LED led_68 (.in(clock_1_out));
  LED led_69 (.in(clock_1_out));
  LED led_70 (.in(clock_1_out));
  LED led_71 (.in(clock_1_out));
  LED led_72 (.in(clock_1_out));
  LED led_73 (.in(clock_1_out));
  LED led_74 (.in(clock_1_out));
  LED led_75 (.in(clock_1_out));
  LED led_76 (.in(clock_1_out));
  and and_1 (and_1_out, or_2_out, decoder_1_out0);
  and and_2 (and_2_out, or_2_out, decoder_1_out1);
  and and_3 (and_3_out, or_2_out, decoder_1_out2);
  and and_4 (and_4_out, or_2_out, decoder_1_out3);
  LED led_77 (.in(clock_1_out));
  LED led_78 (.in(clock_1_out));
  LED led_79 (.in(clock_1_out));
  LED led_80 (.in(clock_1_out));
  LED led_81 (.in(clock_1_out));
  LED led_82 (.in(clock_1_out));
  LED led_83 (.in(clock_1_out));
  LED led_84 (.in(clock_1_out));
  LED led_85 (.in(clock_1_out));
  LED led_86 (.in(clock_1_out));
  LED led_87 (.in(clock_1_out));
  LED led_88 (.in(clock_1_out));
  LED led_89 (.in(clock_1_out));
  LED led_90 (.in(clock_1_out));
  LED led_91 (.in(clock_1_out));
  LED led_92 (.in(clock_1_out));
  LED led_93 (.in(clock_1_out));
  LED led_94 (.in(clock_1_out));
  LED led_95 (.in(clock_1_out));
  LED led_96 (.in(clock_1_out));
  Register register_2 (.D(out_4), .en(and_1_out), .clk(clock_1_out), .Q(register_2_q));  // open: clr
  Register register_3 (.D(out_4), .en(and_2_out), .clk(clock_1_out), .Q(register_3_q));  // open: clr
  Register register_4 (.D(out_4), .en(and_3_out), .clk(clock_1_out), .Q(register_4_q));  // open: clr
  Register register_5 (.D(out_4), .en(and_4_out), .clk(clock_1_out), .Q(register_5_q));  // open: clr
  Adder adder_1 (.a(register_1_q), .b(8'h1), .out(adder_1_out));  // open: cin, cout
  LED led_97 (.in(clock_1_out));
  LED led_98 (.in(clock_1_out));
  LED led_99 (.in(clock_1_out));
  LED led_100 (.in(clock_1_out));
  LED led_101 (.in(clock_1_out));
  LED led_102 (.in(clock_1_out));
  LED led_103 (.in(clock_1_out));
  LED led_104 (.in(clock_1_out));
  LED led_105 (.in(clock_1_out));
  LED led_106 (.in(clock_1_out));
  LED led_107 (.in(clock_1_out));
  LED led_108 (.in(clock_1_out));
  LED led_109 (.in(clock_1_out));
  LED led_110 (.in(clock_1_out));
  LED led_111 (.in(clock_1_out));
  LED led_112 (.in(clock_1_out));
  LED led_113 (.in(clock_1_out));
  LED led_114 (.in(clock_1_out));
  LED led_115 (.in(clock_1_out));
  LED led_116 (.in(clock_1_out));
  LED led_117 (.in(clock_1_out));
  LED led_118 (.in(clock_1_out));
  LED led_119 (.in(clock_1_out));
  LED led_120 (.in(clock_1_out));
  LED led_121 (.in(clock_1_out));
  LED led_122 (.in(clock_1_out));
  LED led_123 (.in(clock_1_out));
  LED led_124 (.in(clock_1_out));
  LED led_125 (.in(clock_1_out));
  LED led_126 (.in(clock_1_out));
  LED led_127 (.in(clock_1_out));
  LED led_128 (.in(clock_1_out));
  LED led_129 (.in(clock_1_out));
  RAM #(.enables("line")) ram_1 (.addr(register_1_q), .clk(clock_1_out), .dout(ram_1_dout));  // open: we, din
  LED led_130 (.in(clock_1_out));
  Multiplexer #(.select(2), .width(8)) multiplexer_1 (
    .in0(register_2_q), .in1(register_3_q), .in2(register_4_q), .in3(register_5_q), .out(out_1),
    .sel(ram_1_dout[1:0]));
  LED led_131 (.in(clock_1_out));
  LED led_132 (.in(clock_1_out));
  LED led_133 (.in(clock_1_out));
  LED led_134 (.in(clock_1_out));
  LED led_135 (.in(clock_1_out));
  LED led_136 (.in(clock_1_out));
  LED led_137 (.in(clock_1_out));
  LED led_138 (.in(clock_1_out));
  LED led_139 (.in(clock_1_out));
  LED led_140 (.in(clock_1_out));
  LED led_141 (.in(clock_1_out));
  LED led_142 (.in(clock_1_out));
  LED led_143 (.in(clock_1_out));
  LED led_144 (.in(clock_1_out));
  LED led_145 (.in(clock_1_out));
  Multiplexer #(.select(2), .width(8)) multiplexer_2 (
    .in0(register_2_q), .in1(register_3_q), .in2(register_4_q), .in3(register_5_q), .out(out_3),
    .sel(ram_1_dout[3:2]));
  Multiplexer #(.select(2), .width(8)) multiplexer_3 (
    .in0(register_2_q), .in1(register_3_q), .in2(register_4_q), .in3(register_5_q), .out(multiplexer_3_out),
    .sel(ram_1_dout[5:4]));
  LED led_146 (.in(clock_1_out));
  LED led_147 (.in(clock_1_out));
  LED led_148 (.in(clock_1_out));
  LED led_149 (.in(clock_1_out));
  LED led_150 (.in(clock_1_out));
  LED led_151 (.in(clock_1_out));
  LED led_152 (.in(clock_1_out));
  LED led_153 (.in(clock_1_out));
  LED led_154 (.in(clock_1_out));
  LED led_155 (.in(clock_1_out));
  LED led_156 (.in(clock_1_out));
  LED led_157 (.in(clock_1_out));
  LED led_158 (.in(clock_1_out));
  LED led_159 (.in(clock_1_out));
  LED led_160 (.in(clock_1_out));
  LED led_161 (.in(clock_1_out));
  LED led_162 (.in(clock_1_out));
  LED led_163 (.in(clock_1_out));
  LED led_164 (.in(clock_1_out));
  LED led_165 (.in(clock_1_out));
  LED led_166 (.in(clock_1_out));
  LED led_167 (.in(clock_1_out));
  LED led_168 (.in(clock_1_out));
  LED led_169 (.in(clock_1_out));
  LED led_170 (.in(clock_1_out));
  LED led_171 (.in(clock_1_out));
  LED led_172 (.in(clock_1_out));
  LED led_173 (.in(clock_1_out));
  LED led_174 (.in(clock_1_out));
  LED led_175 (.in(clock_1_out));
  LED led_176 (.in(clock_1_out));
  LED led_177 (.in(clock_1_out));
  LED led_178 (.in(clock_1_out));
  LED led_179 (.in(clock_1_out));
  LED led_180 (.in(clock_1_out));
  LED led_181 (.in(clock_1_out));
  LED led_182 (.in(clock_1_out));
  LED led_183 (.in(clock_1_out));
  LED led_184 (.in(clock_1_out));
  LED led_185 (.in(clock_1_out));
  LED led_186 (.in(clock_1_out));
  LED led_187 (.in(clock_1_out));
  LED led_188 (.in(clock_1_out));
  LED led_189 (.in(clock_1_out));
  LED led_190 (.in(clock_1_out));
  LED led_191 (.in(clock_1_out));
  LED led_192 (.in(clock_1_out));
  LED led_193 (.in(clock_1_out));
  LED led_194 (.in(clock_1_out));
  LED led_195 (.in(clock_1_out));
  LED led_196 (.in(clock_1_out));
  LED led_197 (.in(clock_1_out));
  LED led_198 (.in(clock_1_out));
  LED led_199 (.in(clock_1_out));
  LED led_200 (.in(clock_1_out));
  LED led_201 (.in(clock_1_out));
  LED led_202 (.in(clock_1_out));
  not not_1 (not_1_out, or_1_out);
  or or_1 (or_1_out, not_2_out, ram_1_dout[6]);
  not not_2 (not_2_out, ram_1_dout[7]);
  LED led_203 (.in(clock_1_out));
  LED led_204 (.in(clock_1_out));
  LED led_205 (.in(clock_1_out));
  LED led_206 (.in(clock_1_out));
  LED led_207 (.in(clock_1_out));
  LED led_208 (.in(clock_1_out));
  LED led_209 (.in(clock_1_out));
  LED led_210 (.in(clock_1_out));
  LED led_211 (.in(clock_1_out));
  LED led_212 (.in(clock_1_out));
  LED led_213 (.in(clock_1_out));
  LED led_214 (.in(clock_1_out));
  LED led_215 (.in(clock_1_out));
  LED led_216 (.in(clock_1_out));
  LED led_217 (.in(clock_1_out));
  LED led_218 (.in(clock_1_out));
  LED led_219 (.in(clock_1_out));
  LED led_220 (.in(clock_1_out));
  LED led_221 (.in(clock_1_out));
  LED led_222 (.in(clock_1_out));
  LED led_223 (.in(clock_1_out));
  LED led_224 (.in(clock_1_out));
  LED led_225 (.in(clock_1_out));
  LED led_226 (.in(clock_1_out));
  LED led_227 (.in(clock_1_out));
  LED led_228 (.in(clock_1_out));
  LED led_229 (.in(clock_1_out));
  LED led_230 (.in(clock_1_out));
  LED led_231 (.in(clock_1_out));
  LED led_232 (.in(clock_1_out));
  Adder adder_2 (.a(out_1), .b(out_3), .out(adder_2_out));  // open: cin, cout
  Multiplier multiplier_1 (.a(out_1), .b(out_3), .out(multiplier_1_out));  // open: cin, cout
  LED led_233 (.in(clock_1_out));
  LED led_234 (.in(clock_1_out));
  LED led_235 (.in(clock_1_out));
  LED led_236 (.in(clock_1_out));
  LED led_237 (.in(clock_1_out));
  LED led_238 (.in(clock_1_out));
  LED led_239 (.in(clock_1_out));
  LED led_240 (.in(clock_1_out));
  LED led_241 (.in(clock_1_out));
  LED led_242 (.in(clock_1_out));
  LED led_243 (.in(clock_1_out));
  Multiplexer #(.width(8)) multiplexer_4 (
    .in0(adder_2_out), .in1(multiplier_1_out), .out(multiplexer_4_out), .sel(not_1_out));
  xor xor_1 (xor_1_out, ram_1_dout[7], ram_1_dout[6]);
  LED led_244 (.in(clock_1_out));
  LED led_245 (.in(clock_1_out));
  LED led_246 (.in(clock_1_out));
  LED led_247 (.in(clock_1_out));
  LED led_248 (.in(clock_1_out));
  LED led_249 (.in(clock_1_out));
  LED led_250 (.in(clock_1_out));
  LED led_251 (.in(clock_1_out));
  LED led_252 (.in(clock_1_out));
  LED led_253 (.in(clock_1_out));
  LED led_254 (.in(clock_1_out));
  LED led_255 (.in(clock_1_out));
  LED led_256 (.in(clock_1_out));
  LED led_257 (.in(clock_1_out));
  LED led_258 (.in(clock_1_out));
  LED led_259 (.in(clock_1_out));
  LED led_260 (.in(clock_1_out));
  LED led_261 (.in(clock_1_out));
  LED led_262 (.in(clock_1_out));
  LED led_263 (.in(clock_1_out));
  LED led_264 (.in(clock_1_out));
  LED led_265 (.in(clock_1_out));
  LED led_266 (.in(clock_1_out));
  LED led_267 (.in(clock_1_out));
  LED led_268 (.in(clock_1_out));
  LED led_269 (.in(clock_1_out));
  LED led_270 (.in(clock_1_out));
  LED led_271 (.in(clock_1_out));
  LED led_272 (.in(clock_1_out));
  LED led_273 (.in(clock_1_out));
  LED led_274 (.in(clock_1_out));
  LED led_275 (.in(clock_1_out));
  LED led_276 (.in(clock_1_out));
  LED led_277 (.in(clock_1_out));
  LED led_278 (.in(clock_1_out));
  LED led_279 (.in(clock_1_out));
  LED led_280 (.in(clock_1_out));
  LED led_281 (.in(clock_1_out));
  LED led_282 (.in(clock_1_out));
  LED led_283 (.in(clock_1_out));
  LED led_284 (.in(clock_1_out));
  LED led_285 (.in(clock_1_out));
  LED led_286 (.in(clock_1_out));
  LED led_287 (.in(clock_1_out));
  LED led_288 (.in(clock_1_out));
  LED led_289 (.in(clock_1_out));
  LED led_290 (.in(clock_1_out));
  LED led_291 (.in(clock_1_out));
  LED led_292 (.in(clock_1_out));
  LED led_293 (.in(clock_1_out));
  LED led_294 (.in(clock_1_out));
  LED led_295 (.in(clock_1_out));
  LED led_296 (.in(clock_1_out));
  LED led_297 (.in(clock_1_out));
  RAM #(.enables("line")) ram_2 (
    .addr(multiplexer_4_out), .we(nor_1_out), .clk(clock_1_out), .din(multiplexer_3_out), .dout(out_2));
  nor nor_1 (nor_1_out, xor_1_out, ram_1_dout[7]);
  or or_2 (or_2_out, xor_1_out, ram_1_dout[7]);
  LED led_298 (.in(clock_1_out));
  LED led_299 (.in(clock_1_out));
  LED led_300 (.in(clock_1_out));
  LED led_301 (.in(clock_1_out));
  LED led_302 (.in(clock_1_out));
  LED led_303 (.in(clock_1_out));
  LED led_304 (.in(clock_1_out));
  LED led_305 (.in(clock_1_out));
  LED led_306 (.in(clock_1_out));
  LED led_307 (.in(clock_1_out));
  LED led_308 (.in(clock_1_out));
  LED led_309 (.in(clock_1_out));
  LED led_310 (.in(clock_1_out));
  LED led_311 (.in(clock_1_out));
  LED led_312 (.in(clock_1_out));
  LED led_313 (.in(clock_1_out));
  LED led_314 (.in(clock_1_out));
  LED led_315 (.in(clock_1_out));
  LED led_316 (.in(clock_1_out));
  LED led_317 (.in(clock_1_out));
  LED led_318 (.in(clock_1_out));
  LED led_319 (.in(clock_1_out));
  LED led_320 (.in(clock_1_out));
  LED led_321 (.in(clock_1_out));
  LED led_322 (.in(clock_1_out));
  LED led_323 (.in(clock_1_out));
  LED led_324 (.in(clock_1_out));
  LED led_325 (.in(clock_1_out));
  LED led_326 (.in(clock_1_out));
  LED led_327 (.in(clock_1_out));
  LED led_328 (.in(clock_1_out));
  LED led_329 (.in(clock_1_out));
  LED led_330 (.in(clock_1_out));
  LED led_331 (.in(clock_1_out));
  LED led_332 (.in(clock_1_out));
  LED led_333 (.in(clock_1_out));
  LED led_334 (.in(clock_1_out));
  LED led_335 (.in(clock_1_out));
  LED led_336 (.in(clock_1_out));
  Multiplexer #(.width(8)) multiplexer_5 (.in0(out_2), .in1(multiplexer_4_out), .out(out_4), .sel(xor_1_out));

  // Notes on the sheet:
  //   Clock
  //   Decoder
  //   WriteReg
  //   RegDataW
  //   Name: Aaditya Kulkarni and Samdarshi Kumar Rai
  //   WriteEnable
  //   Clock
  //   Clock
  //   Clock
  //   Clock
  //   Clock
  //   Pledge: I pledge my honor that I have abided by the Stevens Honor System.
  //   Clock
  //   Instruction Fetching
  //   X0
  //   X1
  //   X2
  //   X3
  //   Execution
  //   output to regdata2
  //   from ReadReg2 to mux
  //   Offset Calculation
  //   ReadReg1
  //   ReadReg2
  //   RegData1
  //   RegData2
  //   ALU
  //   PLUS 01 CROSS 10 LOAD 11 STORE 00
  //   Instruction Decoding
  //   Highly Advised to run the clock on Auto-Tick at 512 Hz or 1024 Hz
  //   mult
  //   writeEnable
  //   Memory Access and Write Back
endmodule
