// Logisim project Machine.circ as structural Verilog: 1 circuit, main circuit main
module main (
  input  [7:0] in_1,
  output [7:0] out_2,
  output [7:0] out_3,
  output [7:0] out_4
);

  wire and_1_out, and_2_out, and_3_out, and_4_out, and_5_out, clock_1_out, decoder_1_out0, decoder_1_out1,
       decoder_1_out2, decoder_1_out3, not_1_out, not_2_out, or_1_out, xor_1_out, xor_2_out, xor_3_out;
  wire [7:0] adder_1_out, adder_2_out, multiplexer_3_out, multiplexer_4_out, multiplier_1_out, ram_1_dout,
       register_1_q, register_2_q, register_3_q, register_4_q, register_5_q, register_6_q;

  Clock clock_1 (.out(clock_1_out));
  LED led_1 ();  // open: in
  Decoder #(.select(2)) decoder_1 (
    .out0(decoder_1_out0), .out1(decoder_1_out1), .out2(decoder_1_out2), .out3(decoder_1_out3),
    .sel({ram_1_dout[0], ram_1_dout[1]}));  // open: en
  LED led_2 (.in(decoder_1_out0));
  LED led_3 (.in(decoder_1_out2));
  LED led_4 ();  // open: in
  Register register_1 (.D(adder_1_out), .en(1'b1), .clk(clock_1_out), .Q(register_1_q));  // open: clr
  LED led_5 ();  // open: in
  and and_1 (and_1_out, or_1_out, decoder_1_out0);
  and and_2 (and_2_out, or_1_out, decoder_1_out1);
  and and_3 (and_3_out, or_1_out, decoder_1_out2);
  and and_4 (and_4_out, or_1_out, decoder_1_out3);
  Register register_2 (.D(in_1), .en(and_1_out), .clk(clock_1_out), .Q(register_2_q));  // open: clr
  Register register_3 (.D(in_1), .en(and_2_out), .clk(clock_1_out), .Q(register_3_q));  // open: clr
  Register register_4 (.D(in_1), .en(and_3_out), .clk(clock_1_out), .Q(register_4_q));  // open: clr
  Register register_5 (.D(in_1), .en(and_4_out), .clk(clock_1_out), .Q(register_5_q));  // open: clr
  Adder adder_1 (.a(register_1_q), .b(8'h1), .out(adder_1_out));  // open: cin, cout
  LED led_6 ();  // open: in
  RAM #(.enables("line")) ram_1 (.addr(register_1_q), .clk(clock_1_out), .dout(ram_1_dout));  // open: we, din
  LED led_7 ();  // open: in
  Multiplexer #(.select(2), .width(8)) multiplexer_1 (
    .in0(register_2_q), .in1(register_3_q), .in2(register_4_q), .in3(register_5_q), .out(out_2),
    .sel({ram_1_dout[4], ram_1_dout[5]}));
  Multiplexer #(.select(2), .width(8)) multiplexer_2 (
    .in0(register_2_q), .in1(register_3_q), .in2(register_4_q), .in3(register_5_q), .out(out_4),
    .sel({ram_1_dout[2], ram_1_dout[3]}));
  Multiplexer #(.width(8)) multiplexer_3 (
    .in0(out_2), .in1({{6{1'b0}}, ram_1_dout[0], ram_1_dout[1]}), .out(multiplexer_3_out), .sel(xor_1_out));
  xor xor_1 (xor_1_out, ram_1_dout[7], ram_1_dout[6]);
  Adder adder_2 (.a(multiplexer_3_out), .b(out_4), .out(adder_2_out));  // open: cin, cout
  Multiplier multiplier_1 (.a(out_2), .b(out_4), .out(multiplier_1_out));  // open: cin, cout
  Multiplexer #(.width(8)) multiplexer_4 (
    .in0(adder_2_out), .in1(multiplier_1_out), .out(multiplexer_4_out), .sel(not_1_out));
  not not_1 (not_1_out, and_5_out);
  xor xor_2 (xor_2_out, ram_1_dout[7], ram_1_dout[6]);
  and and_5 (and_5_out, xor_2_out, ram_1_dout[6]);
  Register register_6 (.D(multiplexer_4_out), .en(1'b1), .clk(clock_1_out), .Q(register_6_q));  // open: clr
  RAM #(.enables("line")) ram_2 (.addr(register_6_q), .we(xor_3_out), .clk(clock_1_out), .din(out_2), .dout(out_3));
  xor xor_3 (xor_3_out, ram_1_dout[7], xor_2_out);
  or or_1 (or_1_out, xor_3_out, not_2_out);
  not not_2 (not_2_out, xor_3_out);
  Multiplexer #(.width(8)) multiplexer_5 (.in0(out_3), .in1(multiplexer_4_out), .out(in_1));  // open: sel

  // Notes on the sheet:
  //   Clock
  //   Decoder
  //   WriteReg
  //   WriteEnable
  //   RegDataW
  //   Name: Aaditya Kulkarni and Samdarshi Kumar Rai
  //   Pledge: I pledge my honor that I have abided by the Stevens Honor System.
  //   Clock
  //   Clock
  //   Clock
  //   Clock
  //   Clock
  //   Clock
  //   X0
  //   X1
  //   X2
  //   X3
  //   output to regdata2
  //   from ReadReg2 to mux
  //   ReadReg1
  //   RegData2
  //   ReadReg2
  //   RegData1
  //   PLUS 01 CROSS 10 LOAD 11 STORE 00
  //   Pluss or mult 
  //   writeEnable
  //   store
  //   mult
  //   load
  //   ReadDataM
endmodule
